// Logisim project p2.circ as structural Verilog
module _6__a_AND_b_AND_C_con_NOR_y_NOT (
  input  in_1,
  input  in_2,
  input  in_3
);

  wire nor_1_out, nor_2_out, not_1_out, not_2_out, not_3_out, not_4_out;

  not not_1 (not_1_out, in_1);
  not not_2 (not_2_out, in_2);
  not not_3 (not_3_out, in_3);
  nor nor_1 (nor_1_out, not_1_out, not_2_out);
  not not_4 (not_4_out, nor_1_out);
  nor nor_2 (nor_2_out, not_4_out, not_3_out);
  LED led_1 (.in(nor_2_out));
endmodule

module _7__Demultiplexor (
  input  c0,
  input  c1,
  input  e0
);

  wire _3_out, and_1_out, and_2_out, and_3_out, and_4_out, not_1_out, not_2_out, s0_out, s1_out, s2_out;

  not not_1 (not_1_out, c0);
  not not_2 (not_2_out, c1);
  and _3 (_3_out, c0, c1);
  and s2 (s2_out, not_1_out, c1);
  and s1 (s1_out, not_2_out, c0);
  and s0 (s0_out, not_1_out, not_2_out);
  LED led_1 (.in(and_1_out));
  and and_1 (and_1_out, _3_out, e0);
  LED led_2 (.in(and_2_out));
  and and_2 (and_2_out, s2_out, e0);
  LED led_3 (.in(and_3_out));
  and and_3 (and_3_out, s1_out, e0);
  LED led_4 (.in(and_4_out));
  and and_4 (and_4_out, s0_out, e0);

  // Notes on the sheet:
  //   s
endmodule

module _8a__Codificador (
  input  e0,
  input  e1,
  input  e2,
  input  e3,
  output s0,
  output s1
);

  wire nor_1_out, nor_2_out, xor_1_out, xor_2_out;

  nor nor_1 (nor_1_out, e0, e1);
  nor nor_2 (nor_2_out, e0, e2);
  xor xor_1 (xor_1_out, e2, e3);
  xor xor_2 (xor_2_out, e1, e3);
  and and_1 (s0, nor_1_out, xor_1_out);
  and and_2 (s1, nor_2_out, xor_2_out);
endmodule
